# Fritzing sketch diagramaElectricoRobot (saved by Fritzing 0.9.3b)
breadboards: 1

parts:
  Arduino_Mega_mini = Arduino Mega 2560 (Rev3)
  Componente2 = Arduino Nano (Rev3.0)
  OLED_I2C1 = OLED 128x64 I2C Monochrome Display
  Componente3 = Adafruit VL530X Time of Flight Distance Sensor [part_number="Adafruit #3317"]
  MPU-1 = Adafruit MPU6050
  Componente4 = Adafruit BH1750 [part_number="Adafruit #4681"]
  Raspberry_Pi_Zero1 = Raspberry Pi Zero
  Raspberry_Pi_1 = Raspberry Pi 3 [part_number=RPI-3-V1.2]
  ENCODER1 = Rotary Encoder with Knob  # not connected
  Componente5 = Logic Level Converter
  VCC1 = Battery  # not connected
  Componente6 = Voltage Sensor 25V  # not connected
  Componente7 = ACS712 Low Current Sensor Board v12  # not connected
  U1 = Voltage Regulator - 5V [package="DPak [SMD]"]  # not connected
  M1 = DC Motor  # not connected
  J1 = Basic Servo  # not connected
  M2 = Stepper Motor - Bipolar  # not connected
  M3 = Stepper Motor - Bipolar  # not connected
  K7 = Relay [part_number=FRS1B-S package=THT]  # not connected
  K8 = Relay [part_number=FRS1B-S package=THT]  # not connected
  K9 = Relay [part_number=FRS1B-S package=THT]  # not connected
  K10 = Relay [part_number=FRS1B-S package=THT]  # not connected
  K11 = Relay [part_number=FRS1B-S package=THT]  # not connected
  K12 = Relay [part_number=FRS1B-S package=THT]  # not connected
  K13 = Relay [part_number=FRS1B-S package=THT]  # not connected
  K14 = Relay [part_number=FRS1B-S package=THT]  # not connected
  K15 = Relay [part_number=FRS1B-S package=THT]  # not connected
  K16 = Relay [part_number=FRS1B-S package=THT]  # not connected
  K17 = Relay [part_number=FRS1B-S package=THT]  # not connected
  K18 = Relay [part_number=FRS1B-S package=THT]  # not connected
  U2 = Voltage Regulator - 5V [package="DPak [SMD]"]  # not connected
  U3 = Voltage Regulator - 5V [package="DPak [SMD]"]  # not connected
  U4 = Voltage Regulator - 5V [package="DPak [SMD]"]  # not connected
  U5 = Voltage Regulator - 5V [package="DPak [SMD]"]  # not connected
  Componente8 = Arduino Mega 2560 (Rev3)

nets:
  N1: Arduino_Mega_mini.D21/SCL, Arduino_Mega_mini.SCL, Componente2.A5, OLED_I2C1.SCK, Componente3.SCL, MPU-1.SCL, Componente4.SCL, Componente5.TX_HV, Componente8.D21/SCL, Componente8.SCL
  N2: Arduino_Mega_mini.D20/SDA, Componente2.A4, OLED_I2C1.SDA, Componente3.SDA, MPU-1.SDA, Componente4.SDA, Componente5.RX_HV, Componente8.D20/SDA, Componente8.SDA
  GND: Arduino_Mega_mini.GND, Componente2.GND, OLED_I2C1.GND, Componente3.GND, MPU-1.GND, Componente4.GND, Raspberry_Pi_Zero1.GND, Raspberry_Pi_1.GND, Componente5.GND, Componente8.GND
  VCC: Arduino_Mega_mini.5V, OLED_I2C1.VDD, Componente3.VCC, MPU-1.VCC, Componente4.VCC, Componente5.HV
  3V3: Raspberry_Pi_Zero1.3v3, Raspberry_Pi_Zero1.3V3, Componente5.LV
  N3: Raspberry_Pi_Zero1.GPIO2, Raspberry_Pi_1.GPIO2, Componente5.RX_LV
  N4: Raspberry_Pi_Zero1.GPIO3, Raspberry_Pi_1.GPIO3, Componente5.TX_LV

custom parts:
  Adafruit VL530X Time of Flight Distance Sensor: The VL53L0X is a Time of Flight distance sensor like no other you've used! The sensor contains a very tiny invisible laser source, and a matching sensor. The VL53L0X can detect the "time of flight", or how long the light has taken to bounce back to the sensor. Since it uses a very narrow light source, it is good for determining distance of only the surface directly in front of it. Unlike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
  Adafruit MPU6050: The MPU-6050 is a popular six axis accelerometer and gyroscope (gyro) that has all the info you need on how things are shakin' and spinnin' . With six axes of sensing and 16-bit measurements, you'll have everything you need to give your robot friend an inner ear. This combination of gyroscopes and accelerometers is commonly referred to as an Inertial Measurement Unit or IMU. Not so long ago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
  Adafruit BH1750: This is the BH1750 16-bit Ambient Light sensor from Rohm. Because of how important it is to humans and most other living things, sensing the amount of light in an environment is a common place to get started when learning to work with microcontrollers and sensors. Should we turn up the brightness of our display or dim it to save power? Which direction should your robot move to stay in an area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
  Rotary Encoder with Knob: Rotary Encoder with 1/4" Shaft and Knob
  Battery: Your standard 2x 18650 battery pack (7,4 Volts)
